# Fritzing sketch BlinkwithLED (saved by Fritzing 0.9.4)
breadboards: 1

parts:
  Teensy_v3_2 = Teensy 3.0  # not connected
  LED_(red) = LED - 5mm [color="Red (633nm)" package="5 mm [THT]"]
  220-Ohm_Resistor_(LED) = Resistor [tolerance=±5% resistance=220 package=THT]

nets:
  N1: LED_(red).anode, 220-Ohm_Resistor_(LED).Pin_1

notes:
  CST8227 - Interfacing
  Lab 02 - Blink
  Discrete red LED.
  Gerald.Hurdle@AlgonquinCollege.com
