# Fritzing sketch Lab6Task1 (saved by Fritzing 0.9.3b)
breadboards: 1

parts:
  Teensy_v3_2 = Teensy 3.1  # not connected
  LED1 = RGB LED (com. cathode, rgb) [package="5 mm [THT]"]
  220-Ohm_Resistor_(Green_LED) = Resistor [tolerance=±5% resistance=220 package="2512 [SMD]"]
  220-Ohm_Resistor_(Blue_LED) = Resistor [tolerance=±5% resistance=220 package="2512 [SMD]"]
  220-Ohm_Resistor_(Red_LED) = Resistor [tolerance=±5% resistance=220 package="2512 [SMD]"]
  Potentiometer = Trimmer Potentiometer [maximum_resistance=10kΩ package=THT]  # not connected

nets:
  N1: LED1.red_anode, 220-Ohm_Resistor_(Red_LED).Pin_0
  N2: LED1.common_cathode, 220-Ohm_Resistor_(Blue_LED).Pin_0
  N3: LED1.blue_anode, 220-Ohm_Resistor_(Green_LED).Pin_0

notes:
  CST8227 – Interfacing
  Lab 06 – User Controlled LED Color
  @author Frank Ngumanenimana
  ngum004@algonqiuinlive.com- CST8227 - Interfacing
