# Fritzing sketch LEDwithPBS-Pull-Up (saved by Fritzing 0.9.4)
breadboards: 1

parts:
  Teensy1 = Teensy 3.0  # not connected
  LED1 = LED - 5mm [color="Red (633nm)" package="5 mm [THT]"]
  R1 = Resistor [tolerance=±5% resistance=220 package=THT]
  S1 = Pushbutton [package="[THT]"]
  R4 = Resistor [tolerance=±5% resistance=10k package=THT]

nets:
  N1: LED1.cathode, S1.Pin_1, S1.Pin_2
  N2: LED1.anode, R1.Pin_1
  N3: S1.Pin_3, S1.Pin_4, R4.Pin_1

notes:
  CST8227 - Interfacing
  Discrete red LED controlled by push-buton switch (PBS) in pull-up configuration.
  Gerald.Hurdle@AlgonquinCollege.com
